// Logisim project ModN_Counter (1).circ as structural Verilog: 1 circuit, main circuit ModN_Counter
module ModN_Counter (
  input  Reset,
  input  N_Limit0,
  input  N_Limit1,
  input  N_Limit2,
  input  N_Limit3,
  output Count_Out0,
  output Count_Out1,
  output Count_Out2,
  output Count_Out3,
  output Terminal_Count
);

  wire a10, a210, CLK, d0, d1, d2, d3, e0, e01, e1, e2, e3, e23, nwrap, nx0, nx1, nx2, nx3, undriven,
       undriven_2, undriven_3, wrap;

  Clock u_CLK (.out(CLK));
  not not_1 (nx0, Count_Out0);
  // XOR_Gate xor_1: pin names not known; wires that end beside it: Count_Out1, Count_Out0, nx1
  and and_1 (a10, Count_Out1, Count_Out0);
  // XOR_Gate xor_2: pin names not known; wires that end beside it: Count_Out2, a10, nx2
  and and_2 (a210, a10, Count_Out2);
  // XOR_Gate xor_3: pin names not known; wires that end beside it: Count_Out3, a210, nx3
  // XNOR_Gate xnor_1: pin names not known; wires that end beside it: nx0, N_Limit0, e0
  // XNOR_Gate xnor_2: pin names not known; wires that end beside it: nx1, N_Limit1, e1
  // XNOR_Gate xnor_3: pin names not known; wires that end beside it: nx2, N_Limit2, e2
  // XNOR_Gate xnor_4: pin names not known; wires that end beside it: nx3, N_Limit3, e3
  and and_3 (e01, e0, e1);
  and and_4 (e23, e2, e3);
  and and_5 (Terminal_Count, e01, e23);
  or or_1 (wrap, Terminal_Count, Reset);
  not not_2 (nwrap, wrap);
  and and_6 (d0, nx0, nwrap);
  and and_7 (d1, nx1, nwrap);
  and and_8 (d2, nx2, nwrap);
  and and_9 (d3, nx3, nwrap);
  D_Flip_Flop d_ff_1 (.clk(d0), .Q(Count_Out0), .reset(undriven));  // open: D, Qn, preset
  D_Flip_Flop d_ff_2 (.clk(d1), .Q(Count_Out1), .preset(undriven), .reset(undriven_2));  // open: D, Qn
  D_Flip_Flop d_ff_3 (.clk(d2), .Q(Count_Out2), .preset(undriven_2), .reset(undriven_3));  // open: D, Qn
  D_Flip_Flop d_ff_4 (.clk(d3), .Q(Count_Out3), .preset(undriven_3));  // open: D, Qn, reset

  // Other names for the same wires on the sheet: Lim0 = N_Limit0; Lim1 = N_Limit1; Lim2 = N_Limit2; Lim3 = N_Limit3;
  //   Q0 = Count_Out0; Q1 = Count_Out1; Q2 = Count_Out2; Q3 = Count_Out3; TC = Terminal_Count

  // Notes on the sheet:
  //   Programmable Mod-N Counter (4-bit)
  //   Counts 0 to N-1. Set N_Limit3..N_Limit0 to N in binary (e.g. 1010 for Mod-10). Reset=1 clears on next clock.
endmodule
