// Logisim project TrafficLightController.circ as structural Verilog: 1 circuit, main circuit TrafficLightController
module TrafficLightController (
  output HW_Red,
  output HW_Yellow,
  output HW_Green,
  output CW_Red,
  output CW_Yellow,
  output CW_Green
);

  wire CLK, not_1_out, nS0, S0, xor_1_p3;

  Clock u_CLK (.out(CLK));
  not not_1 (not_1_out, S0);
  // XOR_Gate xor_1: pin names not known; wires that end beside it: HW_Red, S0, xor_1_p3
  // D_Flip_Flop d_ff_1: pin names not known; wires that end beside it: not_1_out, CLK, S0
  // D_Flip_Flop d_ff_2: pin names not known; wires that end beside it: xor_1_p3, CLK, HW_Red
  not not_2 (CW_Red, HW_Red);
  not not_3 (nS0, S0);
  and and_1 (HW_Yellow, CW_Red, S0);
  // NOR_Gate nor_1: pin names not known; wires that end beside it: HW_Red, S0, HW_Green
  and and_2 (CW_Yellow, HW_Red, S0);
  and and_3 (CW_Green, HW_Red, nS0);

  // Other names for the same wires on the sheet: nS1 = CW_Red; S1 = HW_Red

  // Notes on the sheet:
  //   Traffic Light Controller FSM
  //   States S1S0: 00=HW Green/CW Red, 01=HW Yellow/CW Red, 10=HW Red/CW Green, 11=HW Red/CW Yellow
endmodule
